// Digital circuit main.dig as structural Verilog
module main (
  input  clk,
  input  reset,
  input  [7:0] kb_data,
  input  [12:0] disp_read,
  input  kb_en,
  output [31:0] WB_MUX,
  output [31:0] DISP,
  output [23:0] pc_out
);

  wire BANK_SEL, csr_flags, ctrl_bank_en, ctrl_branch_en, ctrl_csel, ctrl_cycles, ctrl_enc, ctrl_flags_we,
       ctrl_jump_type, ctrl_lut_A, ctrl_lut_B, ctrl_mem_rd, ctrl_mem_wr, ctrl_mul_div_en, ctrl_pc_cond,
       ctrl_pc_link_WE, ctrl_pc_src, ctrl_reg_we, ctrl_shift_op, HALT_IN, ir_addr_a, ir_addr_b, ir_addr_c,
       ir_addr_w, ir_bus, ir_offset, mem_din, mem_rd_out, mul_nxt_enc, nflag_A_zero, pc_link, pc_save, reg_a,
       reg_c, seq_exec, seq_fetch, shift_mul_p_enc;
  wire [1:0] ctrl_sp_out;
  wire [2:0] ctrl_bus_sel, ctrl_wb_sel;
  wire [3:0] ctrl_byte_sel, ctrl_ir_sel;
  wire [9:0] ir_opcode;
  wire [23:0] IR_ADDR, mem_addr, sp_out;
  wire [31:0] alu_out, mem_ram_out, reg_b;

  // alu_control alu_control_1: pin names not known; wires that end beside it: ir_opcode, ctrl_lut_A, ctrl_csel, ctrl_flags_we, ctrl_lut_B, ctrl_shift_op, ctrl_mul_div_en, ctrl_enc
  ir_reg_control ir_reg_control_1 (
    .op(ir_opcode), .ir_imm_sel(ctrl_ir_sel), .wb_sel(ctrl_wb_sel), .reg_we(ctrl_reg_we));
  mem_bus_control mem_bus_control_1 (.op(ir_opcode), .ctrl_bussel(ctrl_bus_sel));
  mem_io_control mem_io_control_1 (
    .op(ir_opcode), .bank_en(ctrl_bank_en), .mem_rd(ctrl_mem_rd), .mem_wr(ctrl_mem_wr),
    .byte_sel(ctrl_byte_sel));
  // pc_control pc_control_1: pin names not known; wires that end beside it: seq_fetch, seq_exec, ir_opcode, ctrl_branch_en, ctrl_jump_type, ctrl_pc_src, ctrl_pc_link_WE, ctrl_cycles, ctrl_pc_cond, ctrl_sp_out, HALT_IN
  // alu_32b_final alu_32b_final_1: pin names not known; wires that end beside it: ctrl_lut_A, ctrl_lut_B, reg_a, ir_bus, reg_c, ctrl_csel, ctrl_flags_we, clk, alu_out, csr_flags
  // register register_1: pin names not known; wires that end beside it: ctrl_reg_we, WB_MUX, ir_addr_a, ir_addr_b, ir_addr_w, seq_exec, clk, BANK_SEL, ctrl_bank_en, ir_addr_c, reg_a, reg_b, reg_c
  // mul_div mul_div_1: pin names not known; wires that end beside it: ir_bus, ctrl_shift_op, ctrl_mul_div_en, reg_a, ctrl_enc, shift_mul_p_enc, nflag_A_zero, mul_nxt_enc
  vga vga_1 (.mem_addr(mem_addr), .mem_din(WB_MUX), .disp_read_addr(disp_read), .clk(clk), .disp_data_out(DISP));
  // ir ir_1: pin names not known; wires that end beside it: mem_din, seq_fetch, clk, ctrl_ir_sel, reg_b, ir_opcode, ir_addr_a, ir_addr_b, ir_addr_w, IR_ADDR, ir_offset, ir_bus, BANK_SEL, ir_addr_c
  RAMDualPort #(.AddrBits(24), .Bits(32)) ramdualport_1 (
    .A(mem_addr), .Din(WB_MUX), .str(ctrl_mem_wr), .C(clk), .ld(mem_rd_out), .D(mem_ram_out));
  // byte_lane_decoder byte_lane_decoder_1: pin names not known; wires that end beside it: mem_ram_out, ctrl_byte_sel, kb_data, mem_din
  // program_counter program_counter_1: pin names not known; wires that end beside it: mem_din, alu_out, ctrl_pc_src, ir_offset, reset, ctrl_cycles, csr_flags, ctrl_pc_cond, ctrl_jump_type, ctrl_branch_en, 1'b1, HALT_IN, kb_en, 1'b1, 1'b1, 1'b1, ctrl_pc_link_WE, clk, pc_out, pc_save, seq_fetch, seq_exec, pc_link
  sp sp_1 (.sp_op(ctrl_sp_out), .CLK(clk), .Reset(reset), .sp_load_in(alu_out), .seq_exec(seq_exec), .sp_out(sp_out));
  // wb_mux wb_mux_1: pin names not known; wires that end beside it: ctrl_wb_sel, alu_out, shift_mul_p_enc, pc_save, mem_din, reg_a, ir_bus, csr_flags, mul_nxt_enc, WB_MUX
  bus_arbitration bus_arbitration_1 (
    .FETCH(seq_fetch), .IR_ADDR(IR_ADDR), .MEM_RD_IN(ctrl_mem_rd), .addr_sel(ctrl_bus_sel), .Reg_b(reg_b),
    .Pc_out(pc_out), .SP_out(sp_out), .Alu_in(alu_out), .ADDR_BUS(mem_addr), .MEM_RD_OUT(mem_rd_out));

  // Other names for the same wires on the sheet: disp_out[31:0] = DISP; disp_read_addr[12:0] = disp_read;
  //   wb_data[31:0] = WB_MUX

  // Notes on the sheet:
  //   Control Unit
  //   ALU
  //   Shift - Encoder
  //   Memory
  //   Instruction Register
  //   Program Counter
  //   Data Bus Switch
endmodule
